# Fritzing sketch six-capsense-terminals (saved by Fritzing 0.8.7b)
breadboards: 1

parts:
  R1 = Resistor [tolerance=±5% resistance=1M package=THT]
  R2 = Resistor [tolerance=±5% resistance=1M package=THT]
  R3 = Resistor [tolerance=±5% resistance=1M package=THT]
  R4 = Resistor [tolerance=±5% resistance=1M package=THT]
  R5 = Resistor [tolerance=±5% resistance=1M package=THT]
  R6 = Resistor [tolerance=±5% resistance=1M package=THT]
  Part1 = Arduino Uno (Rev3)

nets:
  N1: R1.Pin_0, R2.Pin_0, R3.Pin_0, R4.Pin_0, R5.Pin_0, R6.Pin_0, Part1.D12/MISO
  N2: R1.Pin_1, Part1.D6_PWM
  N3: R2.Pin_1, Part1.D8
  N4: R3.Pin_1, Part1.D7
  N5: R4.Pin_1, Part1.D9_PWM
  N6: R5.Pin_1, Part1.D10_PWM/SS
  N7: R6.Pin_1, Part1.D11_PWM/MOSI

notes:
  Attach these wires to small copper pieces
